# Fritzing sketch schematics (saved by Fritzing 0.9.10b)

parts:
  TFT1 = Color 320x240 TFT Display, ILI9341 Controller Chip
  DHT1 = Humidity and Temperature Sensor DHT11
  A1 = Wemos S2 Mini [part_number="WeMos D1 Mini Lite"]
  LED1 = RGB LED (com. cathode, rgb) [package="5 mm [THT]"]

nets:
  VCC: TFT1.VCC, TFT1.LED, DHT1.Vcc, A1.Pin_8, LED1.common_cathode
  N1: TFT1.GND, DHT1.GND_2, A1.Pin_18, A1.Pin_26, LED1.green_anode
  N2: TFT1.CS, A1.Pin_15
  N3: TFT1.Reset, A1.Pin_4
  N4: TFT1.D/C, A1.Pin_2
  N5: TFT1.SDI_(MOSI), A1.Pin_11
  N6: TFT1.SCK, A1.Pin_7
  N7: DHT1.Data-signal, A1.Pin_32
  N8: A1.Pin_30, LED1.red_anode

custom parts:
  Color 320x240 TFT Display, ILI9341 Controller Chip: 2.2" TFT Display with ILI9341 Controller
  Humidity and Temperature Sensor DHT11: Digital relative humidity & temperature sensor DHT11
  Wemos S2 Mini: A mini wifi board based on the ESP32-S2FN4R2.
